// Logisim project Processador.circ as structural Verilog: 10 circuits, main circuit main
module main (
  input  in_1
);

  wire clk, cpu_1_out_8;
  wire [5:0] cpu_1_out_7;
  wire [7:0] cpu_1_out_6, cpu_1_saidas, ram_1_data, ram_2_data;

  Clock clock_1 (.out(clk));
  CPU cpu_1 (
    .in_2(in_1), .in_3(ram_2_data), .in_4(ram_1_data), .SAIDAS(cpu_1_saidas), .out_6(cpu_1_out_6),
    .out_7(cpu_1_out_7), .out_8(cpu_1_out_8), .ENTRADAS(clk));
  RAM #(.bus("separate")) ram_1 (
    .addr(cpu_1_out_6), .din(cpu_1_saidas), .data(ram_1_data), .str(cpu_1_out_8), .clk(clk), .clr(in_1));  // open: sel, ld
  RAM #(.addrWidth(6), .bus("separate")) ram_2 (
    .addr(cpu_1_out_7), .data(ram_2_data));  // open: din, str, sel, clk, ld, clr

  // Other names for the same wires on the sheet: reset = in_1
endmodule

module soma (
  input  [3:0] in_1,
  input  [3:0] in_2,
  input  in_3,
  output [3:0] out_4
);

  wire somacompleta_1_s, somacompleta_2_s, somacompleta_3_s;

  // Probe on in_1
  // Probe on in_2
  somacompleta somacompleta_1 (.x(in_2[2]), .y(in_2[3]), .z(in_3), .s(somacompleta_1_s), .c(out_4[3]));
  somacompleta somacompleta_2 (.x(in_2[0]), .y(in_2[1]), .z(somacompleta_1_s), .s(somacompleta_2_s), .c(out_4[2]));
  somacompleta somacompleta_3 (.x(in_1[2]), .y(in_1[3]), .z(somacompleta_2_s), .s(somacompleta_3_s), .c(out_4[1]));
  somacompleta somacompleta_4 (.x(in_1[0]), .y(in_1[1]), .z(somacompleta_3_s), .c(out_4[0]));  // open: s
  // Probe on out_4
endmodule

module meiasoma (
  input  x,
  input  y,
  output c,
  output s
);

  wire and_2_out, and_3_out, not_1_out, not_2_out;

  and and_1 (c, x, y);
  not not_1 (not_1_out, x);
  not not_2 (not_2_out, y);
  and and_2 (and_2_out, not_1_out, y);
  and and_3 (and_3_out, x, not_2_out);
  or or_1 (s, and_2_out, and_3_out);
endmodule

module somacompleta (
  input  x,
  input  y,
  input  z,
  output s,
  output c
);

  wire meiasoma_1_c, meiasoma_1_s, meiasoma_2_c;

  meiasoma meiasoma_1 (.x(x), .y(y), .c(meiasoma_1_c), .s(meiasoma_1_s));
  meiasoma meiasoma_2 (.x(meiasoma_1_s), .y(z), .c(meiasoma_2_c), .s(c));
  or or_1 (s, meiasoma_1_c, meiasoma_2_c);
endmodule

module ULA (
  input  [7:0] in_1,
  input  [7:0] in_2,
  input  [1:0] in_3,
  output [7:0] out_4,
  output out_5
);

  wire [7:0] adder_1_out, and_1_out, multiplier_1_out, or_1_out;

  Adder adder_1 (.a(in_1), .b(in_2), .out(adder_1_out));  // open: cin, cout
  Multiplier multiplier_1 (.a(in_1), .b(in_2), .out(multiplier_1_out));  // open: cin, cout
  assign and_1_out = in_1 & in_2;  // AND_Gate and_1, 8 bits wide
  assign or_1_out = in_1 | in_2;  // OR_Gate or_1, 8 bits wide
  Comparator comparator_1 (.a(in_1), .b(in_2), .gt(out_5));  // open: eq, lt
  Multiplexer #(.select(2), .width(8)) multiplexer_1 (
    .in0(adder_1_out), .in1(multiplier_1_out), .in2(and_1_out), .in3(or_1_out), .out(out_4), .sel(in_3));  // open: en

  // Other names for the same wires on the sheet: A[7:0] = in_1; B[7:0] = in_2
endmodule

module Latch (
  input  S,
  input  R,
  output Q
);

  wire and_1_out, and_2_out, not_2_out;

  not not_1 (Q, and_1_out);
  and and_1 (and_1_out, S, not_2_out);
  not not_2 (not_2_out, and_2_out);
  and and_2 (and_2_out, Q, R);
endmodule

module FlipFlop (
  input  Input,
  input  Clk,
  input  En,
  input  reset,
  output out_5
);

  wire and_1_out, and_2_out, and_3_out, not_1_out, or_1_out;

  and and_1 (and_1_out, Clk, En);
  and and_2 (and_2_out, Input, and_1_out);
  and and_3 (and_3_out, and_1_out, not_1_out);
  not not_1 (not_1_out, Input);
  or or_1 (or_1_out, and_3_out, reset);
  Latch latch_1 (.S(and_2_out), .R(or_1_out), .Q(out_5));
endmodule

module register (
  input  clk,
  input  \input ,
  input  en,
  input  reset,
  output out_5
);

  wire flipflop_1_out_5, not_1_out;

  FlipFlop flipflop_1 (.Input(\input ), .Clk(clk), .En(en), .reset(reset), .out_5(flipflop_1_out_5));
  not not_1 (not_1_out, clk);
  FlipFlop flipflop_2 (.Input(flipflop_1_out_5), .Clk(not_1_out), .En(en), .reset(reset), .out_5(out_5));
endmodule

module REGS (
  input  [1:0] adda,
  input  [1:0] addb,
  input  [7:0] \input ,
  input  clk,
  input  reset,
  input  en,
  output [7:0] outa,
  output [7:0] outb
);

  wire en0, en1, en2, en3;
  wire [7:0] q0, q1, q2, q3;

  Demultiplexer #(.select(2)) demultiplexer_1 (
    .out0(en0), .out1(en1), .out2(en2), .out3(en3), .in(en), .sel(adda));  // open: en
  Register register_1 (.D(\input ), .en(en0), .Q(q0), .clk(clk), .clr(reset));
  Register register_2 (.D(\input ), .en(en2), .Q(q2), .clk(clk), .clr(reset));
  Register register_3 (.D(\input ), .en(en1), .Q(q1), .clk(clk), .clr(reset));
  Register register_4 (.D(\input ), .en(en3), .Q(q3), .clk(clk), .clr(reset));
  Multiplexer #(.select(2), .width(8)) multiplexer_1 (
    .in0(q0), .in1(q1), .in2(q2), .in3(q3), .out(outa), .sel(adda));  // open: en
  Multiplexer #(.select(2), .width(8)) multiplexer_2 (
    .in0(q0), .in1(q1), .in2(q2), .in3(q3), .out(outb), .sel(addb));  // open: en
endmodule

module CPU (
  input  ENTRADAS,
  input  in_2,
  input  [7:0] in_3,
  input  [7:0] in_4,
  output [7:0] SAIDAS,
  output [7:0] out_6,
  output [5:0] out_7,
  output out_8
);

  wire and_10_out, cmp, isAdd, isAnd, isCmp, isLdr, isMov, isMul, isOr, isSpecialCase, isStr, movecons,
       not_1_out, not_2_out, not_3_out, not_4_out, not_5_out, not_6_out, not_7_out, not_8_out, not_9_out,
       not_10_out, not_11_out, not_12_out, not_13_out, not_14_out, not_15_out, not_16_out, not_17_out,
       not_18_out, not_19_out, not_20_out, not_21_out, not_22_out, regen, ula_1_out_5;
  wire [1:0] multiplexer_3_out, op;
  wire [5:0] adder_1_out, nextline;
  wire [7:0] multiplexer_1_out, multiplexer_2_out, multiplexer_4_out, outula;
  wire [7:7] constant;

  Register #(.width(6)) register_1 (.D(nextline), .en(ENTRADAS), .Q(out_7), .clk(ENTRADAS), .clr(in_2));
  Multiplexer #(.width(8)) multiplexer_1 (
    .in0(outula), .in1({{6{constant[7]}}, in_3[1:0]}), .out(multiplexer_1_out), .sel(movecons));  // open: en
  Multiplexer #(.width(8)) multiplexer_2 (
    .in0(multiplexer_1_out), .in1(out_6), .out(multiplexer_2_out), .sel(isMov));  // open: en
  Multiplexer #(.width(2)) multiplexer_3 (
    .in0(in_3[1:0]), .in1(2'b11), .out(multiplexer_3_out), .sel(isSpecialCase));  // open: en
  Multiplexer #(.width(8)) multiplexer_4 (
    .in0(multiplexer_2_out), .in1(in_4), .out(multiplexer_4_out), .sel(isLdr));  // open: en
  not not_1 (not_1_out, in_3[5]);
  not not_2 (not_2_out, in_3[6]);
  not not_3 (not_3_out, in_3[7]);
  not not_4 (not_4_out, in_3[4]);
  not not_5 (not_5_out, in_3[6]);
  not not_6 (not_6_out, in_3[7]);
  not not_7 (not_7_out, in_3[4]);
  not not_8 (not_8_out, in_3[7]);
  REGS regs_1 (
    .adda(multiplexer_3_out), .addb(in_3[3:2]), .\input (multiplexer_4_out), .clk(ENTRADAS), .reset(in_2),
    .en(regen), .outa(SAIDAS), .outb(out_6));
  Subtractor #(.width(2)) subtractor_1 (.a(in_3[5:4]), .b(2'b01), .out(op));  // open: bin, bout
  and and_1 (isAdd, in_3[4], not_1_out, not_2_out, not_3_out);
  and and_2 (isMul, not_4_out, in_3[5], not_5_out, not_6_out);
  and and_3 (isMov, not_7_out, in_3[5], in_3[6], not_8_out);
  ULA ula_1 (.in_1(SAIDAS), .in_2(out_6), .out_4(outula), .out_5(ula_1_out_5), .in_3(op));
  // Probe on outula
  Register #(.width(1)) register_2 (.D(ula_1_out_5), .en(isCmp), .Q(cmp), .clk(ENTRADAS), .clr(in_2));
  not not_9 (not_9_out, in_3[2]);
  not not_10 (not_10_out, in_3[3]);
  not not_11 (not_11_out, in_3[7]);
  and and_4 (isAnd, in_3[4], in_3[5], not_12_out, not_13_out);
  not not_12 (not_12_out, in_3[6]);
  not not_13 (not_13_out, in_3[7]);
  not not_14 (not_14_out, in_3[4]);
  and and_5 (isOr, not_14_out, not_15_out, in_3[6], not_16_out);
  not not_15 (not_15_out, in_3[5]);
  not not_16 (not_16_out, in_3[7]);
  and and_6 (isCmp, in_3[4], not_17_out, in_3[6], not_18_out);
  not not_17 (not_17_out, in_3[5]);
  not not_18 (not_18_out, in_3[7]);
  or or_1 (isSpecialCase, movecons, isStr, isLdr);
  or or_2 (regen, isLdr, isAdd, isMul, movecons, isAnd, isOr, isMov);
  and and_7 (movecons, not_9_out, not_10_out, in_3[4], in_3[5], in_3[6], not_11_out);
  not not_19 (not_19_out, in_3[3]);
  not not_20 (not_20_out, in_3[7]);
  not not_21 (not_21_out, in_3[2]);
  not not_22 (not_22_out, in_3[7]);
  and and_8 (isStr, in_3[2], not_19_out, in_3[4], in_3[5], in_3[6], not_20_out);
  and and_9 (isLdr, not_21_out, in_3[3], in_3[4], in_3[5], in_3[6], not_22_out);
  Adder #(.width(6)) adder_1 (.a(out_7), .b(6'b000001), .out(adder_1_out));  // open: cin, cout
  Multiplexer #(.width(6)) multiplexer_5 (
    .in0(adder_1_out), .in1(in_3[5:0]), .out(nextline), .sel(and_10_out));  // open: en
  and and_10 (and_10_out, in_3[7], cmp);

  // Other names for the same wires on the sheet: address[5:0] = in_3[5:0]; opcode[7:0] = in_3; addb[1:0] = in_3[3:2];
  //   clk = ENTRADAS; adda[1:0] = in_3[1:0]; constant[6:0] = {{5{constant[7]}}, in_3[1:0]}; memoryout[7:0] = in_4;
  //   isJmp = in_3[7]; memoryin[7:0] = SAIDAS; outA[7:0] = SAIDAS; memoryadd[7:0] = out_6; outB[7:0] = out_6;
  //   PC[5:0] = out_7; reset = in_2; str = out_8
endmodule
